// Logisim project Calculadora Digital.circ as structural Verilog
module somador (
  input  A0,
  input  A1,
  input  A2,
  input  A3,
  input  B0,
  input  B1,
  input  B2,
  input  B3,
  output S0,
  output S1,
  output S2,
  output S3,
  output Carry
);

  wire somador_completo_1_carry, somador_completo_2_carry, somador_completo_2_soma, somador_completo_4_carry,
       somador_completo_4_soma, somador_completo_5_soma;

  somador_completo somador_completo_1 (.A(A0), .B(B0), .Soma(S0), .Carry(somador_completo_1_carry));
  somador_completo somador_completo_2 (
    .A(somador_completo_1_carry), .B(A1), .Soma(somador_completo_2_soma), .Carry(somador_completo_2_carry));
  somador_completo somador_completo_3 (.A(somador_completo_2_soma), .B(B1), .Soma(S1));  // open: Carry
  somador_completo somador_completo_4 (
    .A(somador_completo_2_carry), .B(A2), .Soma(somador_completo_4_soma), .Carry(somador_completo_4_carry));
  somador_completo somador_completo_5 (
    .A(somador_completo_4_carry), .B(A3), .Soma(somador_completo_5_soma), .Carry(Carry));
  somador_completo somador_completo_6 (.A(somador_completo_4_soma), .B(B2), .Soma(S2));  // open: Carry
  somador_completo somador_completo_7 (.A(somador_completo_5_soma), .B(B3), .Soma(S3));  // open: Carry
endmodule

module multiplexador (
  input  in_1,
  input  in_2
);
endmodule

module somador_completo (
  input  A,
  input  B,
  output Soma,
  output Carry
);

  xor xor_1 (Soma, A, B);
  and and_1 (Carry, A, B);
endmodule
